// Logisim project 2-1.circ as structural Verilog: 1 circuit, main circuit main
module main (
  input  up_0_down_1,
  input  I0,
  input  S,
  input  D,
  input  Sel,
  input  I1,
  input  D_2,
  input  clk,
  input  clock,
  output q1,
  output q2,
  output q3,
  output q0,
  output Q,
  output Z,
  output nQ,
  output Q2_2,
  output out_18,
  output out_19
);

  wire adder_1_out, adder_2_out, adder_3_out, and_1_out, and_2_out, and_3_out, and_4_out, and_5_out,
       and_6_out, d_ff_1_qn, d_ff_2_qn, d_ff_3_qn, multiplexer_1_out, not_1_out, not_2_out, not_3_out,
       not_4_out, or_1_out, or_2_out, or_3_out, reset_out;

  not not_1 (not_1_out, up_0_down_1);
  not not_2 (not_2_out, q0);
  Button reset (.out(reset_out));
  D_Flip_Flop d_ff_1 (.D(not_2_out), .clk(clock), .Q(q0), .Qn(d_ff_1_qn), .reset(reset_out));  // open: preset
  and and_1 (and_1_out, d_ff_1_qn, up_0_down_1);
  and and_2 (and_2_out, not_1_out, q0);
  or or_1 (or_1_out, and_2_out, and_1_out);
  D_Flip_Flop d_ff_2 (.D(adder_1_out), .clk(clock), .Q(q1), .Qn(d_ff_2_qn), .reset(reset_out));  // open: preset
  Adder #(.width(1)) adder_1 (.a(q1), .b(or_1_out), .out(adder_1_out));  // open: cin, cout
  and and_3 (and_3_out, and_2_out, q1);
  and and_4 (and_4_out, d_ff_2_qn, and_1_out);
  or or_2 (or_2_out, and_3_out, and_4_out);
  D_Flip_Flop d_ff_3 (.D(adder_2_out), .clk(clock), .Q(q2), .Qn(d_ff_3_qn), .reset(reset_out));  // open: preset
  Adder #(.width(1)) adder_2 (.a(q2), .b(or_2_out), .out(adder_2_out));  // open: cin, cout
  and and_5 (and_5_out, d_ff_3_qn, and_4_out);
  and and_6 (and_6_out, and_3_out, q2);
  D_Flip_Flop d_ff_4 (.D(adder_3_out), .clk(clock), .Q(q3), .reset(reset_out));  // open: Qn, preset
  Adder #(.width(1)) adder_3 (.a(q3), .b(or_3_out), .out(adder_3_out));  // open: cin, cout
  or or_3 (or_3_out, and_6_out, and_5_out);
  not not_3 (not_3_out, S);
  Multiplexer multiplexer_1 (.in0(multiplexer_1_out), .in1(D_2), .out(multiplexer_1_out), .sel(not_4_out));
  not not_4 (not_4_out, clk);
  // Transmission_Gate transmission_1: pin names not known; wires that end beside it: I0, S, not_3_out, Z
  // Transmission_Gate transmission_2: pin names not known; wires that end beside it: I1, not_3_out, S, Z
  not not_5 (out_19, multiplexer_1_out);
  Multiplexer multiplexer_2 (.in0(Q2_2), .in1(multiplexer_1_out), .out(Q2_2), .sel(clk));
  not not_6 (out_18, Q2_2);
  Multiplexer multiplexer_3 (.in0(Q), .in1(D), .out(Q), .sel(Sel));
  not not_7 (nQ, Q);

  // Notes on the sheet:
  //   counter
  //   mux
  //   D-flip-flop
  //   Q1
  //   Latch
endmodule
