// Logisim project 2-2.circ as structural Verilog: 1 circuit, main circuit main
module main (
);

  wire and_1_out, and_2_out, and_3_out, and_4_out, and_5_out, button_1_out, clock_1_out, comparator_1_eq,
       comparator_1_gt, d_ff_1_q, decoder_1_out7, decoder_1_out8, decoder_1_out9, decoder_1_out10,
       decoder_1_out11, decoder_1_out12, decoder_1_out13, decoder_1_out14, decoder_1_out15,
       multiplexer_3_out, not_1_out, not_2_out, not_3_out, not_4_out, not_6_out, or_1_out, or_2_out,
       or_3_out, or_4_out, w1_LDA, w2_SUB, w3_ADD, w4_JGE, w5_JNE, w6_JMP, w7_STP, w8_STO;
  wire [3:0] bit_extender_1_out, multiplexer_2_out, multiplexer_2_out_2, multiplexer_2_out_3, register_1_q,
       register_1_q_2, register_1_q_3;
  wire [11:0] adder_1_out, demultiplexer_1_out0, demultiplexer_1_out1, multiplexer_1_out;
  wire [15:0] adder_2_out, multiplexer_4_out, multiplexer_5_out, multiplexer_6_out, not_5_out, ram_1_dout,
       register_2_q, register_3_q, rom_1_data;

  not not_1 (not_1_out, d_ff_1_q);
  Button button_1 (.out(button_1_out));
  Clock clock_1 (.out(clock_1_out));
  D_Flip_Flop d_ff_1 (.D(not_1_out), .clk(clock_1_out), .Q(d_ff_1_q), .reset(button_1_out));  // open: Qn, preset
  or or_1 (or_1_out, and_5_out, w6_JMP, and_4_out);
  Adder #(.width(12)) adder_1 (
    .a({register_1_q_3, register_1_q_2, register_1_q}), .b({12{1'b0}}), .out(adder_1_out), .cin(1'b1));  // open: cout
  or or_2 (or_2_out, and_4_out, w6_JMP, and_5_out, d_ff_1_q);
  not not_2 (not_2_out, d_ff_1_q);
  Hex_Digit_Display hex_digit_display_1 (.value(register_1_q_3));  // open: dp
  Hex_Digit_Display hex_digit_display_2 (.value(register_1_q_2));  // open: dp
  Multiplexer #(.width(12)) multiplexer_1 (
    .in0(adder_1_out), .in1(register_3_q[11:0]), .out(multiplexer_1_out), .sel(or_1_out));
  and and_1 (and_1_out, or_2_out, w7_STP);
  Hex_Digit_Display hex_digit_display_3 (.value(register_1_q));  // open: dp
  Register #(.width(12)) register_1 (
    .D(multiplexer_1_out), .en(and_1_out), .clk(clock_1_out),
    .Q({register_1_q_3, register_1_q_2, register_1_q}), .clr(button_1_out));
  Hex_Digit_Display hex_digit_display_4 (.value(multiplexer_2_out_3));  // open: dp
  Multiplexer #(.width(12)) multiplexer_2 (
    .in0({register_1_q_3, register_1_q_2, register_1_q}), .in1(register_3_q[11:0]),
    .out({multiplexer_2_out_3, multiplexer_2_out_2, multiplexer_2_out}), .sel(d_ff_1_q));
  not not_3 (not_3_out, clock_1_out);
  Hex_Digit_Display hex_digit_display_5 (.value(multiplexer_2_out_2));  // open: dp
  Hex_Digit_Display hex_digit_display_6 (.value(multiplexer_2_out));  // open: dp
  and and_2 (and_2_out, w8_STO, not_3_out, d_ff_1_q);
  not not_4 (not_4_out, multiplexer_2_out_3[3]);
  Demultiplexer #(.width(12)) demultiplexer_1 (
    .out0(demultiplexer_1_out0), .out1(demultiplexer_1_out1),
    .in({multiplexer_2_out_3, multiplexer_2_out_2, multiplexer_2_out}), .sel(not_4_out));
  Multiplexer multiplexer_3 (.in0(1'b0), .in1(1'b1), .out(multiplexer_3_out), .sel(w2_SUB));
  RAM #(.addrWidth(12), .asyncread("true"), .clearpin("true"), .dataWidth(16)) ram_1 (
    .addr(demultiplexer_1_out0), .we(and_2_out), .oe(1'b1), .clk(clock_1_out), .din(register_2_q),
    .dout(ram_1_dout), .clr(button_1_out));
  ROM #(.addrWidth(12), .dataWidth(16)) rom_1 (.addr(demultiplexer_1_out1), .data(rom_1_data));
  Multiplexer #(.width(16)) multiplexer_4 (.in0(register_2_q), .in1({16{1'b0}}), .out(multiplexer_4_out), .sel(w1_LDA));
  Multiplexer #(.width(16)) multiplexer_5 (
    .in0(multiplexer_6_out), .in1(not_5_out), .out(multiplexer_5_out), .sel(multiplexer_3_out));
  assign not_5_out = ~multiplexer_6_out;  // NOT_Gate not_5, 16 bits wide
  // Probe on multiplexer_4_out
  Adder #(.width(16)) adder_2 (
    .a(multiplexer_4_out), .b(multiplexer_5_out), .out(adder_2_out), .cin(multiplexer_3_out));  // open: cout
  // Probe on multiplexer_5_out
  // Probe on adder_2_out
  or or_3 (or_3_out, w1_LDA, w2_SUB, w3_ADD);
  Multiplexer #(.width(16)) multiplexer_6 (
    .in0(ram_1_dout), .in1(rom_1_data), .out(multiplexer_6_out), .sel(not_4_out));
  Register #(.width(16)) register_2 (
    .D(adder_2_out), .en(and_3_out), .clk(clock_1_out), .Q(register_2_q), .clr(button_1_out));
  and and_3 (and_3_out, or_3_out, d_ff_1_q);
  Comparator #(.width(16)) comparator_1 (
    .a(register_2_q), .b({16{1'b0}}), .gt(comparator_1_gt), .eq(comparator_1_eq));  // open: lt
  Hex_Digit_Display hex_digit_display_7 (.value(register_2_q[15:12]));  // open: dp
  Register #(.width(16)) register_3 (
    .D(multiplexer_6_out), .en(not_2_out), .clk(clock_1_out), .Q(register_3_q), .clr(button_1_out));
  or or_4 (or_4_out, comparator_1_gt, comparator_1_eq);
  not not_6 (not_6_out, comparator_1_eq);
  Hex_Digit_Display hex_digit_display_8 (.value(register_2_q[11:8]));  // open: dp
  Hex_Digit_Display hex_digit_display_9 (.value(register_2_q[7:4]));  // open: dp
  Hex_Digit_Display hex_digit_display_10 (.value(register_2_q[3:0]));  // open: dp
  Hex_Digit_Display hex_digit_display_11 (.value(register_3_q[15:12]));  // open: dp
  assign bit_extender_1_out = {{3{1'b0}}, d_ff_1_q};  // Bit_Extender bit_extender_1
  and and_4 (and_4_out, or_4_out, w4_JGE);
  and and_5 (and_5_out, not_6_out, w5_JNE);
  Decoder #(.select(4)) decoder_1 (
    .out0(w1_LDA), .out1(w8_STO), .out2(w3_ADD), .out3(w2_SUB), .out4(w6_JMP), .out5(w4_JGE), .out6(w5_JNE),
    .out7(decoder_1_out7), .out8(decoder_1_out8), .out9(decoder_1_out9), .out10(decoder_1_out10),
    .out11(decoder_1_out11), .out12(decoder_1_out12), .out13(decoder_1_out13), .out14(decoder_1_out14),
    .out15(decoder_1_out15), .sel(register_3_q[15:12]));  // open: en
  Hex_Digit_Display hex_digit_display_12 (.value(bit_extender_1_out));  // open: dp
  nor nor_1 (w7_STP, decoder_1_out7, decoder_1_out8, decoder_1_out9, decoder_1_out10, decoder_1_out11, decoder_1_out12, decoder_1_out13, decoder_1_out14, decoder_1_out15);

  // Notes on the sheet:
  //   Reset
  //   Clock
  //   Program Counter
  //   PC
  //   Memory Address
  //   contents of rom_1 (hex, n*v repeats v):
  //   400 2400 1800 401 2402 3403 1801 4010 7000 600 3600 616 2600 1803 6000 7000 500 2501 5008 3501 1802
  //   5009 7000 1001*0 20 5555 aa 55 252*0 7fff 1 254*0 1234
  //   Load Image: MU0_ram.txt
  //   ACC
  //   IR
  //   Accumulator Value
  //   OpCode
  //   Machine State
endmodule
